# Fritzing sketch GeeDee_Wiring (saved by Fritzing 0.9.2b)
breadboards: 1

parts:
  Part1 = HC-SR04 Ultrasonic Rangemeter
  Part2 = Pro Trinket 5V
  VCC1 = 4 x AAA Battery Mount
  J1 = Basic Servo
  J2 = Basic Servo

nets:
  VCC: Part1.VCC, Part2.VBAT, VCC1.+, J1.vcc, J2.vcc
  N1: Part1.Trig, Part2.D13
  N2: Part1.Echo, Part2.D12
  GND: Part1.GND, Part2.GND, VCC1.-, J1.gnd, J2.gnd
  N3: Part2.D9, J1.pulse
  N4: Part2.D10, J2.pulse

custom parts:
  Pro Trinket 5V: The Pro Trinket 5V is like an Arduino Pro Mini with more pins and USB included. Built with the common core Arduino chip, the ATmega328p, it has 18 GPIO, 2 extra analog inputs, 28K of flash, and 2K of RAM. It has onboard USB bootloading support with Optiboot support, so you can either program your Pro Trinket over USB or with a FTDI cable. The Pro Trinket is programmable using the Arduino IDE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
